# Fritzing sketch esp_mpu_circuit (saved by Fritzing 0.9.3b)
breadboards: 1

parts:
  Power_plug1_3_3V = Power plug
  R1 = Resistor [tolerance=±5% resistance=330k package=THT]
  R2 = Resistor [tolerance=±5% resistance=330 package=THT]
  R3 = Resistor [tolerance=±5% resistance=3.3k package=THT]
  R4 = Resistor [tolerance=±5% resistance=330 package=THT]
  R5 = Resistor [tolerance=±5% resistance=330 package=THT]
  S1 = Pushbutton [package="[THT]"]
  Pullup = Resistor [tolerance=±5% resistance=3.3k package=THT]
  GY1 = MPU-6050 Board GY-521 [form="♀ (female)" package=THT]
  U1 = ESP8266 WiFi Module [part_number=ESP8266]

nets:
  N1: Power_plug1_3_3V.VCC, R1.Pin_0, R3.Pin_0, Pullup.Pin_0, GY1.pin1, U1.GPIO_0, U1.GPIO_2, U1.CH_PD
  N2: Power_plug1_3_3V.GND, S1.Pin_3, S1.Pin_4, GY1.pin2
  N3: R1.Pin_1, R2.Pin_1, GY1.pin4
  N4: R2.Pin_0, U1.TXD
  N5: R3.Pin_1, R4.Pin_1, GY1.pin3
  N6: R4.Pin_0, R5.Pin_1, U1.RXD
  N7: S1.Pin_1, S1.Pin_2, Pullup.Pin_1, U1.RST

notes:
  Press RST switch to reset the device so it starts a new.
  Connect GPIO 0 VCC esp when wanting to operate ESP.
  Connect GPIO 0 GND ESP when wanting to flash the firmware. When flashing the firmware press RST switch before starting the flashing process.

custom parts:
  MPU-6050 Board GY-521: Acelerometro y Giroscopio MPU-6050 Board GY-521
  ESP8266 WiFi Module: Generic WiFi Module based on the ESP8266 with onboard PCB antenna and UART communications
